# Fritzing sketch system_circuitry (saved by Fritzing 0.8.7b)
breadboards: 1

parts:
  VALVE1 = Plastic Solenoid Valve
  S4 = Magnetic Door Switch [package=reed_switch_plastic]
  U1 = NodeMCU V1.0
  R2 = Photocell (LDR) [package=THT]
  부품2 = FC-28 Soil Hygrometer Module - Probe
  U2 = RELAY [package=relay-t9a-2]
  R3 = Resistor [tolerance=±5% resistance=220 package=THT]
  U3 = CD74HC4067 [package=ssop24]
  RHT1 = Humidity and Temperature Sensor RHT03
  D1 = SOLAR-IXYS [package=solarbit-12x1]
  R4 = Heating Pad
  BT1 = Bluetooth HC-06u [package=THT]

nets:
  N1: VALVE1.no_name_yet#1, S4.1, 부품2.NEG, U2.COIL1, R3.Pin_1, RHT1.GND_1, D1.C
  N2: VALVE1.no_name_yet#2, U1.D5
  N3: S4.2, U1.D6
  N4: U1.D0, U3.S0
  N5: U1.D1, U3.S1
  N6: U1.D2, U3.S2
  N7: U1.D3, U3.S3
  N8: U1.D4, RHT1.Data-signal
  N9: U1.D7, U2.COIL2
  N10: U1.RX, BT1.TXD
  N11: U1.TX, BT1.RXD
  N12: U1.A0, U3.COM
  N13: R2.pin_0, RHT1.Vcc, D1.A
  N14: R2.pin_1, R3.Pin_0, U3.CHAN0
  N15: 부품2.POS, U3.CHAN1
  N16: U2.NO, R4.pin_0
  GND: U3.GND, U3.EN, BT1.GND
  VCC: U3.VCC, BT1.VCC

notes:
  Solar Cell
  16 Analog Multiplexer
  Circuitry for Each Room
  Door Switch Magnet
  Solenoid Valve
  Assumed Soil Salinity Sensor
  LDR
  DHT21
  Heating Pad(Heater)
  Relay for Heater
  Bluetooth Module

custom parts:
  NodeMCU V1.0: ESP8266 based NodeMCU
  FC-28 Soil Hygrometer Module - Probe: The FC-28 is a soil hygrometer module that uses the Texas Instruments LM393 comparator chip to provide an analog measurement of soil humidity.
  CD74HC4067: 16-channel analog MUX
  Heating Pad: A thermoresistant material with an embeded conductor that dissipates electrical energy into heat.
  Bluetooth HC-06u: Bluetooth HC-06 - face up, pins down 16.5mm x 37.5mm PCB
