# Fritzing sketch sensors (saved by Fritzing 0.8.7b)
breadboards: 1

parts:
  R1 = Photocell (LDR) [package=THT]
  J1 = Basic Servo
  LED1 = LED - 5mm [color="Red (633nm)" package="5 mm [THT]"]
  R2 = Resistor [tolerance=±5% resistance=220 package=THT]
  R3 = Resistor [package="2512 [SMD]"]
  LED2 = LED - 5mm [color="Red (633nm)" package="5 mm [THT]"]
  R4 = Resistor [package="2512 [SMD]"]
  RHT1 = Humidity and Temperature Sensor RHT03
  U1 = NodeMCU V1.0

nets:
  VCC: R1.pin_0, J1.vcc, RHT1.Vcc, U1.3V3
  N1: R1.pin_1, R2.Pin_0, U1.A0
  GND: J1.gnd, R2.Pin_1, R3.Pin_0, R4.Pin_0, RHT1.GND_1, U1.GND
  N2: J1.pulse, U1.D2
  N3: LED1.cathode, R3.Pin_1
  N4: LED1.anode, U1.D0
  N5: LED2.cathode, R4.Pin_1
  N6: LED2.anode, U1.D1
  N7: RHT1.Data-signal, U1.D4

custom parts:
  NodeMCU V1.0: ESP8266 based NodeMCU
